// Logisim project Graph Calculator Mark 4 17.circ as structural Verilog: 2 circuits, main circuit main
module main (
  input  [1:0] in_1,
  input  [3:0] in_2,
  input  [3:0] in_3,
  input  [3:0] in_4
);

  wire button_1_out, cdm_8_1_p2, cdm_8_1_p4, cdm_8_1_p5, cdm_8_1_p6, cdm_8_1_p7, cdm_8_1_p8, cdm_8_1_p9, Cl,
       code, Coef1Button, Coef2Button, Coef3Button, comparator_1_gt, comparator_2_gt, comparator_3_gt,
       comparator_4_eq, comparator_5_eq, comparator_6_eq, comparator_7_gt, comparator_8_eq, comparator_9_eq,
       comparator_10_eq, comparator_11_eq, comparator_12_eq, comparator_13_eq, comparator_14_eq,
       comparator_15_eq, comparator_16_eq, comparator_17_eq, comparator_18_eq, comparator_19_eq,
       comparator_20_eq, comparator_21_eq, comparator_22_eq, comparator_23_eq, comparator_24_eq,
       comparator_25_eq, comparator_26_eq, comparator_27_eq, comparator_28_eq, comparator_29_eq,
       comparator_30_eq, comparator_31_eq, comparator_32_eq, comparator_33_eq, comparator_34_eq,
       comparator_35_eq, comparator_36_eq, comparator_37_eq, comparator_38_eq, comparator_39_eq,
       comparator_40_eq, comparator_41_eq, comparator_42_eq, comparator_43_eq, comparator_44_eq,
       comparator_45_eq, comparator_46_eq, comparator_47_eq, comparator_48_eq, comparator_49_eq,
       comparator_50_eq, comparator_51_eq, comparator_52_eq, comparator_53_eq, comparator_54_eq,
       comparator_55_eq, comparator_56_eq, comparator_57_eq, comparator_58_eq, comparator_59_eq,
       comparator_60_eq, comparator_61_eq, comparator_62_eq, comparator_63_eq, comparator_64_eq,
       comparator_65_eq, comparator_66_eq, comparator_67_eq, comparator_68_eq, comparator_69_eq,
       comparator_70_eq, comparator_71_eq, comparator_72_eq, comparator_73_eq, data, I_Osel, In_out_prime,
       mem, nand_1_out, not_1_out, not_2_out, not_3_out, not_4_out, not_5_out, not_6_out, not_7_out, RAM,
       trig_1, trig_2, trig_2_1, trig_2_2, trig_2_3, trig_2_4, trig_2_5, trig_2_6, trig_2_7, trig_2_8,
       trig_2_9, trig_2_10, trig_2_11, trig_2_12, trig_2_13, trig_2_14, trig_2_15, trig_2_16, trig_2_17,
       trig_2_18, trig_2_19, trig_2_20, trig_2_21, trig_2_22, trig_2_23, trig_2_24, trig_2_25, trig_2_26,
       trig_2_27, trig_2_28, trig_2_29, trig_2_30, trig_2_31, trig_2_32, trig_3, trig_4, trig_5, trig_6,
       trig_7, trig_8, trig_9, trig_10, trig_11, trig_12, trig_13, trig_14, trig_15, trig_16, trig_17,
       trig_18, trig_19, trig_20, trig_21, trig_22, trig_23, trig_24, trig_25, trig_26, trig_27, trig_28,
       trig_29, trig_30, trig_31, trig_32;
  wire [1:0] adder_4_out, multiplexer_7_out, register_4_q;
  wire [3:0] adder_1_out, adder_2_out, adder_3_out, Coef1, Coef2, Coef3, I_Oadr, multiplexer_1_out,
       multiplexer_2_out, multiplexer_3_out, multiplexer_4_out, multiplexer_5_out, multiplexer_6_out,
       multiplexer_8_out;
  wire [7:0] adder_5_out, cdm_8_1_p13, cdm_8_1_p14, data_pass, I_Odat, register_5_q, register_6_q,
       register_8_q, x_counter;
  wire [7:4] cdm_8_1_p12;
  wire [31:0] data_pass_translated_down, data_pass_translated_up, led1_1, led1_2, led1_3, led1_4, led1_5,
       led1_6, led1_7, led1_8, led1_9, led1_10, led1_11, led1_12, led1_13, led1_14, led1_15, led1_16,
       led1_17, led1_18, led1_19, led1_20, led1_21, led1_22, led1_23, led1_24, led1_25, led1_26, led1_27,
       led1_28, led1_29, led1_30, led1_31, led1_32, led2_1, led2_2, led2_3, led2_4, led2_5, led2_6, led2_7,
       led2_8, led2_9, led2_10, led2_11, led2_12, led2_13, led2_14, led2_15, led2_16, led2_17, led2_18,
       led2_19, led2_20, led2_21, led2_22, led2_23, led2_24, led2_25, led2_26, led2_27, led2_28, led2_29,
       led2_30, led2_31, led2_32, led3_1, led3_2, led3_3, led3_4, led3_5, led3_6, led3_7, led3_8, led3_9,
       led3_10, led3_11, led3_12, led3_13, led3_14, led3_15, led3_16, led3_17, led3_18, led3_19, led3_20,
       led3_21, led3_22, led3_23, led3_24, led3_25, led3_26, led3_27, led3_28, led3_29, led3_30, led3_31,
       led3_32, led4_1, led4_2, led4_3, led4_4, led4_5, led4_6, led4_7, led4_8, led4_9, led4_10, led4_11,
       led4_12, led4_13, led4_14, led4_15, led4_16, led4_17, led4_18, led4_19, led4_20, led4_21, led4_22,
       led4_23, led4_24, led4_25, led4_26, led4_27, led4_28, led4_29, led4_30, led4_31, led4_32,
       multiplexer_9_out, multiplexer_10_out, multiplexer_11_out, multiplexer_12_out, multiplexer_13_out,
       multiplexer_14_out, multiplexer_15_out, multiplexer_16_out, multiplexer_17_out, multiplexer_18_out,
       multiplexer_19_out, multiplexer_20_out, multiplexer_21_out, multiplexer_22_out, multiplexer_23_out,
       multiplexer_24_out, multiplexer_25_out, multiplexer_26_out, multiplexer_27_out, multiplexer_28_out,
       multiplexer_29_out, multiplexer_30_out, multiplexer_31_out, multiplexer_32_out, multiplexer_33_out,
       multiplexer_34_out, multiplexer_35_out, multiplexer_36_out, multiplexer_37_out, multiplexer_38_out,
       multiplexer_39_out, multiplexer_40_out, multiplexer_41_out, multiplexer_42_out, multiplexer_43_out,
       multiplexer_44_out, multiplexer_45_out, multiplexer_46_out, multiplexer_47_out, multiplexer_48_out,
       multiplexer_49_out, multiplexer_50_out, multiplexer_51_out, multiplexer_52_out, multiplexer_53_out,
       multiplexer_54_out, multiplexer_55_out, multiplexer_56_out, multiplexer_57_out, multiplexer_58_out,
       multiplexer_59_out, multiplexer_60_out, multiplexer_61_out, multiplexer_62_out, multiplexer_63_out,
       multiplexer_64_out, multiplexer_65_out, multiplexer_66_out, multiplexer_67_out, multiplexer_68_out,
       multiplexer_69_out, multiplexer_70_out, multiplexer_71_out, multiplexer_72_out, multiplexer_73_out,
       multiplexer_74_out, multiplexer_75_out, multiplexer_76_out, multiplexer_77_out, multiplexer_78_out,
       multiplexer_79_out, multiplexer_80_out, multiplexer_81_out, multiplexer_82_out, multiplexer_83_out,
       multiplexer_84_out, multiplexer_85_out, multiplexer_86_out, multiplexer_87_out, multiplexer_88_out,
       multiplexer_89_out, multiplexer_90_out, multiplexer_91_out, multiplexer_92_out, multiplexer_93_out,
       multiplexer_94_out, multiplexer_95_out, multiplexer_96_out, multiplexer_97_out, multiplexer_98_out,
       multiplexer_99_out, multiplexer_100_out, multiplexer_101_out, multiplexer_102_out,
       multiplexer_103_out, multiplexer_104_out, multiplexer_105_out, multiplexer_106_out,
       multiplexer_107_out, multiplexer_108_out, multiplexer_109_out, multiplexer_110_out,
       multiplexer_111_out, multiplexer_112_out, multiplexer_113_out, multiplexer_114_out,
       multiplexer_115_out, multiplexer_116_out, multiplexer_117_out, multiplexer_118_out,
       multiplexer_119_out, multiplexer_120_out, multiplexer_121_out, multiplexer_122_out,
       multiplexer_123_out, multiplexer_124_out, multiplexer_125_out, multiplexer_126_out,
       multiplexer_127_out, multiplexer_128_out, multiplexer_129_out, multiplexer_130_out,
       multiplexer_131_out, multiplexer_132_out, multiplexer_133_out, multiplexer_134_out,
       multiplexer_135_out, multiplexer_136_out;

  Clock clock_1 (.out(Cl));
  Comparator #(.width(4), .mode("unsigned")) comparator_1 (.a(Coef2), .b(in_3), .gt(comparator_1_gt));  // open: eq, lt
  Comparator #(.width(4), .mode("unsigned")) comparator_2 (.a(Coef3), .b(in_4), .gt(comparator_2_gt));  // open: eq, lt
  // Probe on cdm_8_1_p4
  // Probe on cdm_8_1_p2
  // Probe on cdm_8_1_p5
  // Probe on cdm_8_1_p6
  Button button_1 (.out(button_1_out));
  and and_1 (I_Osel, not_4_out, Cl, data);
  Comparator #(.width(4), .mode("unsigned")) comparator_3 (.a(Coef1), .b(in_2), .gt(comparator_3_gt));  // open: eq, lt
  Multiplexer #(.width(4), .enable("false")) multiplexer_1 (
    .in0(4'b0001), .in1(4'b0000), .out(multiplexer_1_out), .sel(not_1_out));
  not not_1 (not_1_out, Coef1Button);
  Multiplexer #(.width(4), .enable("false")) multiplexer_2 (
    .in0(in_2), .in1(Coef1), .out(multiplexer_2_out), .sel(comparator_3_gt));
  Multiplexer #(.width(4), .enable("false")) multiplexer_3 (
    .in0(4'b0001), .in1(4'b0000), .out(multiplexer_3_out), .sel(not_2_out));
  Multiplexer #(.width(4), .enable("false")) multiplexer_4 (
    .in0(in_3), .in1(Coef2), .out(multiplexer_4_out), .sel(comparator_1_gt));
  not not_2 (not_2_out, Coef2Button);
  Multiplexer #(.width(4), .enable("false")) multiplexer_5 (
    .in0(4'b0001), .in1(4'b0000), .out(multiplexer_5_out), .sel(not_3_out));
  Multiplexer #(.width(4), .enable("false")) multiplexer_6 (
    .in0(in_4), .in1(Coef3), .out(multiplexer_6_out), .sel(comparator_2_gt));
  not not_3 (not_3_out, Coef3Button);
  // Probe on cdm_8_1_p8
  // Probe on cdm_8_1_p7
  not not_4 (not_4_out, nand_1_out);
  // Probe on Coef1
  Adder #(.width(4)) adder_1 (.a(multiplexer_1_out), .b(multiplexer_2_out), .out(adder_1_out));  // open: cin, cout
  Comparator #(.width(4)) comparator_4 (.a(Coef1), .b(4'b1010), .eq(comparator_4_eq));  // open: gt, lt
  // Probe on Coef2
  Adder #(.width(4)) adder_2 (.a(multiplexer_3_out), .b(multiplexer_4_out), .out(adder_2_out));  // open: cin, cout
  Comparator #(.width(4)) comparator_5 (.a(Coef2), .b(4'b1010), .eq(comparator_5_eq));  // open: gt, lt
  // Probe on Coef3
  Adder #(.width(4)) adder_3 (.a(multiplexer_5_out), .b(multiplexer_6_out), .out(adder_3_out));  // open: cin, cout
  Comparator #(.width(4)) comparator_6 (.a(Coef3), .b(4'b1010), .eq(comparator_6_eq));  // open: gt, lt
  // CdM_8 cdm_8_1: pin names not known; wires that end beside it: Cl, cdm_8_1_p2, button_1_out, cdm_8_1_p4, cdm_8_1_p5, cdm_8_1_p6, cdm_8_1_p7, cdm_8_1_p8, cdm_8_1_p9, mem, In_out_prime, {cdm_8_1_p12, I_Oadr}, cdm_8_1_p13, cdm_8_1_p14
  nand nand_1 (nand_1_out, cdm_8_1_p12[4], cdm_8_1_p12[5], cdm_8_1_p12[6], cdm_8_1_p12[7]);
  and and_2 (RAM, nand_1_out, data);
  Register #(.width(4), .trigger("falling")) register_1 (
    .D(adder_1_out), .Q(Coef1), .clk(Coef1Button), .clr(comparator_4_eq));  // open: en
  Register #(.width(4), .trigger("falling")) register_2 (
    .D(adder_2_out), .Q(Coef2), .clk(Coef2Button), .clr(comparator_5_eq));  // open: en
  Register #(.width(4), .trigger("falling")) register_3 (
    .D(adder_3_out), .Q(Coef3), .clk(Coef3Button), .clr(comparator_6_eq));  // open: en
  assign cdm_8_1_p14 = In_out_prime ? I_Odat : 8'bz;  // Controlled_Buffer controlled_buffer_1
  Decoder #(.disabled(0)) decoder_1 (.out0(code), .out1(data), .sel(cdm_8_1_p9), .en(mem));
  assign I_Odat = not_5_out ? cdm_8_1_p13 : 8'bz;  // Controlled_Buffer controlled_buffer_2
  not not_5 (not_5_out, In_out_prime);
  Comparator #(.width(2), .mode("unsigned")) comparator_7 (
    .a(in_1), .b(register_4_q), .gt(comparator_7_gt));  // open: eq, lt
  // Probe on I_Odat
  // Probe on I_Odat
  // Probe on Coef2
  // Probe on Coef1
  Multiplexer #(.width(2), .enable("false")) multiplexer_7 (
    .in0(in_1), .in1(register_4_q), .out(multiplexer_7_out), .sel(not_6_out));
  not not_6 (not_6_out, comparator_7_gt);
  Comparator comparator_8 (.a(data_pass), .b(register_5_q), .eq(comparator_8_eq));  // open: gt, lt
  not not_7 (not_7_out, Cl);
  // Probe on Coef3
  Register #(.width(2), .trigger("falling")) register_4 (
    .D(adder_4_out), .Q(register_4_q), .clk(I_Osel));  // open: en, clr
  Adder #(.width(2)) adder_4 (.a(multiplexer_7_out), .b(2'b01), .out(adder_4_out));  // open: cin, cout
  Comparator comparator_9 (.a(8'hab), .b(I_Odat), .eq(comparator_9_eq));  // open: gt, lt
  Register #(.trigger("high")) register_5 (
    .D(I_Odat), .en(comparator_9_eq), .Q(register_5_q), .clk(comparator_9_eq));  // open: clr
  Register register_6 (.D(adder_5_out), .en(comparator_8_eq), .Q(register_6_q), .clk(comparator_8_eq));  // open: clr
  Adder adder_5 (.a(register_6_q), .b(8'h1), .out(adder_5_out));  // open: cin, cout
  ROM rom_1 (.addr({cdm_8_1_p12, I_Oadr}), .data(I_Odat), .sel(code));
  RAM ram_1 (.addr({cdm_8_1_p12, I_Oadr}), .data(I_Odat), .sel(RAM), .clk(not_7_out), .ld(In_out_prime));  // open: clr
  Multiplexer #(.select(2), .width(4), .enable("false")) multiplexer_8 (
    .in0(Coef1), .in1(Coef2), .in2(Coef3), .out(multiplexer_8_out), .sel(register_4_q));  // open: in3
  Register #(.trigger("high")) register_7 (.D(register_5_q), .en(I_Osel), .Q(data_pass), .clk(I_Osel));  // open: clr
  Register register_8 (.D({4'b0000, multiplexer_8_out}), .Q(register_8_q), .clk(In_out_prime));  // open: en, clr
  assign I_Odat = I_Osel ? register_8_q : 8'bz;  // Controlled_Buffer controlled_buffer_3
  // Probe on x_counter
  Adder adder_6 (.a({8{1'b1}}), .b(register_6_q), .out(x_counter));  // open: cin, cout
  DotMatrix #(.matrixcols(32), .matrixrows(32)) dotmatrix_1 (
    .col0(led1_32), .col1(led1_31), .col2(led1_30), .col3(led1_29), .col4(led1_28), .col5(led1_27),
    .col6(led1_26), .col7(led1_25), .col8(led1_24), .col9(led1_23), .col10(led1_22), .col11(led1_21),
    .col12(led1_20), .col13(led1_19), .col14(led1_18), .col15(led1_17), .col16(led1_16), .col17(led1_15),
    .col18(led1_14), .col19(led1_13), .col20(led1_12), .col21(led1_11), .col22(led1_10), .col23(led1_9),
    .col24(led1_8), .col25(led1_7), .col26(led1_6), .col27(led1_5), .col28(led1_4), .col29(led1_3),
    .col30(led1_2), .col31(led1_1));
  DotMatrix #(.matrixcols(32), .matrixrows(32)) dotmatrix_2 (
    .col0(led2_32), .col1(led2_31), .col2(led2_30), .col3(led2_29), .col4(led2_28), .col5(led2_27),
    .col6(led2_26), .col7(led2_25), .col8(led2_24), .col9(led2_23), .col10(led2_22), .col11(led2_21),
    .col12(led2_20), .col13(led2_19), .col14(led2_18), .col15(led2_17), .col16(led2_16), .col17(led2_15),
    .col18(led2_14), .col19(led2_13), .col20(led2_12), .col21(led2_11), .col22(led2_10), .col23(led2_9),
    .col24(led2_8), .col25(led2_7), .col26(led2_6), .col27(led2_5), .col28(led2_4), .col29(led2_3),
    .col30(led2_2), .col31(led2_1));
  Hex_Digit_Display hex_digit_display_1 (.value(Coef1));  // open: dp
  Button button_2 (.out(Coef1Button));
  Hex_Digit_Display hex_digit_display_2 (.value(Coef2));  // open: dp
  Button button_3 (.out(Coef2Button));
  DotMatrix #(.matrixcols(32), .matrixrows(32)) dotmatrix_3 (
    .col0(led3_1), .col1(led3_2), .col2(led3_3), .col3(led3_4), .col4(led3_5), .col5(led3_6), .col6(led3_7),
    .col7(led3_8), .col8(led3_9), .col9(led3_10), .col10(led3_11), .col11(led3_12), .col12(led3_13),
    .col13(led3_14), .col14(led3_15), .col15(led3_16), .col16(led3_17), .col17(led3_18), .col18(led3_19),
    .col19(led3_20), .col20(led3_21), .col21(led3_22), .col22(led3_23), .col23(led3_24), .col24(led3_25),
    .col25(led3_26), .col26(led3_27), .col27(led3_28), .col28(led3_29), .col29(led3_30), .col30(led3_32),
    .col31(led3_31));
  DotMatrix #(.matrixcols(32), .matrixrows(32)) dotmatrix_4 (
    .col0(led4_1), .col1(led4_2), .col2(led4_3), .col3(led4_4), .col4(led4_5), .col5(led4_6), .col6(led4_7),
    .col7(led4_8), .col8(led4_9), .col9(led4_10), .col10(led4_11), .col11(led4_12), .col12(led4_13),
    .col13(led4_14), .col14(led4_15), .col15(led4_16), .col16(led4_17), .col17(led4_18), .col18(led4_19),
    .col19(led4_20), .col20(led4_21), .col21(led4_22), .col22(led4_23), .col23(led4_24), .col24(led4_25),
    .col25(led4_26), .col26(led4_27), .col27(led4_28), .col28(led4_29), .col29(led4_30), .col30(led4_31),
    .col31(led4_32));
  Hex_Digit_Display hex_digit_display_3 (.value(Coef3));  // open: dp
  Button button_4 (.out(Coef3Button));
  Comparator comparator_10 (.a(8'h1), .b(data_pass), .eq(comparator_10_eq));  // open: gt, lt
  Comparator comparator_11 (.a(8'h2), .b(data_pass), .eq(comparator_11_eq));  // open: gt, lt
  Comparator comparator_12 (.a(8'h3), .b(data_pass), .eq(comparator_12_eq));  // open: gt, lt
  Comparator comparator_13 (.a(8'h4), .b(data_pass), .eq(comparator_13_eq));  // open: gt, lt
  Comparator comparator_14 (.a(8'h5), .b(data_pass), .eq(comparator_14_eq));  // open: gt, lt
  Comparator comparator_15 (.a(8'h6), .b(data_pass), .eq(comparator_15_eq));  // open: gt, lt
  Comparator comparator_16 (.a(8'h7), .b(data_pass), .eq(comparator_16_eq));  // open: gt, lt
  Comparator comparator_17 (.a(8'h8), .b(data_pass), .eq(comparator_17_eq));  // open: gt, lt
  Comparator comparator_18 (.a(8'h9), .b(data_pass), .eq(comparator_18_eq));  // open: gt, lt
  Comparator comparator_19 (.a(8'ha), .b(data_pass), .eq(comparator_19_eq));  // open: gt, lt
  Comparator comparator_20 (.a(8'hb), .b(data_pass), .eq(comparator_20_eq));  // open: gt, lt
  Comparator comparator_21 (.a(8'hc), .b(data_pass), .eq(comparator_21_eq));  // open: gt, lt
  Comparator comparator_22 (.a(8'hd), .b(data_pass), .eq(comparator_22_eq));  // open: gt, lt
  Comparator comparator_23 (.a(8'he), .b(data_pass), .eq(comparator_23_eq));  // open: gt, lt
  Comparator comparator_24 (.a(8'hf), .b(data_pass), .eq(comparator_24_eq));  // open: gt, lt
  Comparator comparator_25 (.a(8'h10), .b(data_pass), .eq(comparator_25_eq));  // open: gt, lt
  Comparator comparator_26 (.a(8'h11), .b(data_pass), .eq(comparator_26_eq));  // open: gt, lt
  Comparator comparator_27 (.a(8'h12), .b(data_pass), .eq(comparator_27_eq));  // open: gt, lt
  Comparator comparator_28 (.a(8'h13), .b(data_pass), .eq(comparator_28_eq));  // open: gt, lt
  Comparator comparator_29 (.a(8'h14), .b(data_pass), .eq(comparator_29_eq));  // open: gt, lt
  Comparator comparator_30 (.a(8'h15), .b(data_pass), .eq(comparator_30_eq));  // open: gt, lt
  Comparator comparator_31 (.a(8'h16), .b(data_pass), .eq(comparator_31_eq));  // open: gt, lt
  Comparator comparator_32 (.a(8'h17), .b(data_pass), .eq(comparator_32_eq));  // open: gt, lt
  Comparator comparator_33 (.a(8'h18), .b(data_pass), .eq(comparator_33_eq));  // open: gt, lt
  Comparator comparator_34 (.a(8'h19), .b(data_pass), .eq(comparator_34_eq));  // open: gt, lt
  Comparator comparator_35 (.a(8'h1a), .b(data_pass), .eq(comparator_35_eq));  // open: gt, lt
  Comparator comparator_36 (.a(8'h1b), .b(data_pass), .eq(comparator_36_eq));  // open: gt, lt
  Comparator comparator_37 (.a(8'h1c), .b(data_pass), .eq(comparator_37_eq));  // open: gt, lt
  Comparator comparator_38 (.a(8'h1d), .b(data_pass), .eq(comparator_38_eq));  // open: gt, lt
  Comparator comparator_39 (.a(8'h1e), .b(data_pass), .eq(comparator_39_eq));  // open: gt, lt
  Comparator comparator_40 (.a(8'h1f), .b(data_pass), .eq(comparator_40_eq));  // open: gt, lt
  Comparator comparator_41 (.a(8'h20), .b(data_pass), .eq(comparator_41_eq));  // open: gt, lt
  // Probe on data_pass_translated_up
  assign data_pass_translated_up = comparator_10_eq ? 32'h1 : 32'bz;  // Controlled_Buffer controlled_buffer_4
  assign data_pass_translated_up = comparator_11_eq ? 32'h2 : 32'bz;  // Controlled_Buffer controlled_buffer_5
  assign data_pass_translated_up = comparator_12_eq ? 32'h4 : 32'bz;  // Controlled_Buffer controlled_buffer_6
  assign data_pass_translated_up = comparator_13_eq ? 32'h8 : 32'bz;  // Controlled_Buffer controlled_buffer_7
  assign data_pass_translated_up = comparator_14_eq ? 32'h10 : 32'bz;  // Controlled_Buffer controlled_buffer_8
  assign data_pass_translated_up = comparator_15_eq ? 32'h20 : 32'bz;  // Controlled_Buffer controlled_buffer_9
  assign data_pass_translated_up = comparator_16_eq ? 32'h40 : 32'bz;  // Controlled_Buffer controlled_buffer_10
  assign data_pass_translated_up = comparator_17_eq ? 32'h80 : 32'bz;  // Controlled_Buffer controlled_buffer_11
  assign data_pass_translated_up = comparator_18_eq ? 32'h100 : 32'bz;  // Controlled_Buffer controlled_buffer_12
  assign data_pass_translated_up = comparator_19_eq ? 32'h200 : 32'bz;  // Controlled_Buffer controlled_buffer_13
  assign data_pass_translated_up = comparator_20_eq ? 32'h400 : 32'bz;  // Controlled_Buffer controlled_buffer_14
  assign data_pass_translated_up = comparator_21_eq ? 32'h800 : 32'bz;  // Controlled_Buffer controlled_buffer_15
  assign data_pass_translated_up = comparator_22_eq ? 32'h1000 : 32'bz;  // Controlled_Buffer controlled_buffer_16
  assign data_pass_translated_up = comparator_23_eq ? 32'h2000 : 32'bz;  // Controlled_Buffer controlled_buffer_17
  assign data_pass_translated_up = comparator_24_eq ? 32'h4000 : 32'bz;  // Controlled_Buffer controlled_buffer_18
  assign data_pass_translated_up = comparator_25_eq ? 32'h8000 : 32'bz;  // Controlled_Buffer controlled_buffer_19
  assign data_pass_translated_up = comparator_26_eq ? 32'h10000 : 32'bz;  // Controlled_Buffer controlled_buffer_20
  assign data_pass_translated_up = comparator_27_eq ? 32'h20000 : 32'bz;  // Controlled_Buffer controlled_buffer_21
  assign data_pass_translated_up = comparator_28_eq ? 32'h40000 : 32'bz;  // Controlled_Buffer controlled_buffer_22
  assign data_pass_translated_up = comparator_29_eq ? 32'h80000 : 32'bz;  // Controlled_Buffer controlled_buffer_23
  assign data_pass_translated_up = comparator_30_eq ? 32'h100000 : 32'bz;  // Controlled_Buffer controlled_buffer_24
  assign data_pass_translated_up = comparator_31_eq ? 32'h200000 : 32'bz;  // Controlled_Buffer controlled_buffer_25
  assign data_pass_translated_up = comparator_32_eq ? 32'h400000 : 32'bz;  // Controlled_Buffer controlled_buffer_26
  assign data_pass_translated_up = comparator_33_eq ? 32'h800000 : 32'bz;  // Controlled_Buffer controlled_buffer_27
  assign data_pass_translated_up = comparator_34_eq ? 32'h1000000 : 32'bz;  // Controlled_Buffer controlled_buffer_28
  assign data_pass_translated_up = comparator_35_eq ? 32'h2000000 : 32'bz;  // Controlled_Buffer controlled_buffer_29
  assign data_pass_translated_up = comparator_36_eq ? 32'h4000000 : 32'bz;  // Controlled_Buffer controlled_buffer_30
  assign data_pass_translated_up = comparator_37_eq ? 32'h8000000 : 32'bz;  // Controlled_Buffer controlled_buffer_31
  assign data_pass_translated_up = comparator_38_eq ? 32'h10000000 : 32'bz;  // Controlled_Buffer controlled_buffer_32
  assign data_pass_translated_up = comparator_39_eq ? 32'h20000000 : 32'bz;  // Controlled_Buffer controlled_buffer_33
  assign data_pass_translated_up = comparator_40_eq ? 32'h40000000 : 32'bz;  // Controlled_Buffer controlled_buffer_34
  assign data_pass_translated_up = comparator_41_eq ? 32'h80000000 : 32'bz;  // Controlled_Buffer controlled_buffer_35
  // Probe on data_pass_translated_down
  Comparator comparator_42 (.a(8'he0), .b(data_pass), .eq(comparator_42_eq));  // open: gt, lt
  assign data_pass_translated_down = comparator_42_eq ? 32'h1 : 32'bz;  // Controlled_Buffer controlled_buffer_36
  Comparator comparator_43 (.a(8'he1), .b(data_pass), .eq(comparator_43_eq));  // open: gt, lt
  assign data_pass_translated_down = comparator_43_eq ? 32'h2 : 32'bz;  // Controlled_Buffer controlled_buffer_37
  Comparator comparator_44 (.a(8'he2), .b(data_pass), .eq(comparator_44_eq));  // open: gt, lt
  assign data_pass_translated_down = comparator_44_eq ? 32'h4 : 32'bz;  // Controlled_Buffer controlled_buffer_38
  Comparator comparator_45 (.a(8'he3), .b(data_pass), .eq(comparator_45_eq));  // open: gt, lt
  assign data_pass_translated_down = comparator_45_eq ? 32'h8 : 32'bz;  // Controlled_Buffer controlled_buffer_39
  Comparator comparator_46 (.a(8'he4), .b(data_pass), .eq(comparator_46_eq));  // open: gt, lt
  assign data_pass_translated_down = comparator_46_eq ? 32'h10 : 32'bz;  // Controlled_Buffer controlled_buffer_40
  Comparator comparator_47 (.a(8'he5), .b(data_pass), .eq(comparator_47_eq));  // open: gt, lt
  assign data_pass_translated_down = comparator_47_eq ? 32'h20 : 32'bz;  // Controlled_Buffer controlled_buffer_41
  Comparator comparator_48 (.a(8'he6), .b(data_pass), .eq(comparator_48_eq));  // open: gt, lt
  assign data_pass_translated_down = comparator_48_eq ? 32'h40 : 32'bz;  // Controlled_Buffer controlled_buffer_42
  Comparator comparator_49 (.a(8'he7), .b(data_pass), .eq(comparator_49_eq));  // open: gt, lt
  assign data_pass_translated_down = comparator_49_eq ? 32'h80 : 32'bz;  // Controlled_Buffer controlled_buffer_43
  Comparator comparator_50 (.a(8'he8), .b(data_pass), .eq(comparator_50_eq));  // open: gt, lt
  assign data_pass_translated_down = comparator_50_eq ? 32'h100 : 32'bz;  // Controlled_Buffer controlled_buffer_44
  Comparator comparator_51 (.a(8'he9), .b(data_pass), .eq(comparator_51_eq));  // open: gt, lt
  assign data_pass_translated_down = comparator_51_eq ? 32'h200 : 32'bz;  // Controlled_Buffer controlled_buffer_45
  Comparator comparator_52 (.a(8'hea), .b(data_pass), .eq(comparator_52_eq));  // open: gt, lt
  assign data_pass_translated_down = comparator_52_eq ? 32'h400 : 32'bz;  // Controlled_Buffer controlled_buffer_46
  Comparator comparator_53 (.a(8'heb), .b(data_pass), .eq(comparator_53_eq));  // open: gt, lt
  assign data_pass_translated_down = comparator_53_eq ? 32'h800 : 32'bz;  // Controlled_Buffer controlled_buffer_47
  Comparator comparator_54 (.a(8'hec), .b(data_pass), .eq(comparator_54_eq));  // open: gt, lt
  assign data_pass_translated_down = comparator_54_eq ? 32'h1000 : 32'bz;  // Controlled_Buffer controlled_buffer_48
  Comparator comparator_55 (.a(8'hed), .b(data_pass), .eq(comparator_55_eq));  // open: gt, lt
  assign data_pass_translated_down = comparator_55_eq ? 32'h2000 : 32'bz;  // Controlled_Buffer controlled_buffer_49
  Comparator comparator_56 (.a(8'hee), .b(data_pass), .eq(comparator_56_eq));  // open: gt, lt
  assign data_pass_translated_down = comparator_56_eq ? 32'h4000 : 32'bz;  // Controlled_Buffer controlled_buffer_50
  Comparator comparator_57 (.a(8'hef), .b(data_pass), .eq(comparator_57_eq));  // open: gt, lt
  assign data_pass_translated_down = comparator_57_eq ? 32'h8000 : 32'bz;  // Controlled_Buffer controlled_buffer_51
  Comparator comparator_58 (.a(8'hf0), .b(data_pass), .eq(comparator_58_eq));  // open: gt, lt
  assign data_pass_translated_down = comparator_58_eq ? 32'h10000 : 32'bz;  // Controlled_Buffer controlled_buffer_52
  Comparator comparator_59 (.a(8'hf1), .b(data_pass), .eq(comparator_59_eq));  // open: gt, lt
  assign data_pass_translated_down = comparator_59_eq ? 32'h20000 : 32'bz;  // Controlled_Buffer controlled_buffer_53
  Comparator comparator_60 (.a(8'hf2), .b(data_pass), .eq(comparator_60_eq));  // open: gt, lt
  assign data_pass_translated_down = comparator_60_eq ? 32'h40000 : 32'bz;  // Controlled_Buffer controlled_buffer_54
  Comparator comparator_61 (.a(8'hf3), .b(data_pass), .eq(comparator_61_eq));  // open: gt, lt
  assign data_pass_translated_down = comparator_61_eq ? 32'h80000 : 32'bz;  // Controlled_Buffer controlled_buffer_55
  Comparator comparator_62 (.a(8'hf4), .b(data_pass), .eq(comparator_62_eq));  // open: gt, lt
  assign data_pass_translated_down = comparator_62_eq ? 32'h100000 : 32'bz;  // Controlled_Buffer controlled_buffer_56
  Comparator comparator_63 (.a(8'hf5), .b(data_pass), .eq(comparator_63_eq));  // open: gt, lt
  assign data_pass_translated_down = comparator_63_eq ? 32'h200000 : 32'bz;  // Controlled_Buffer controlled_buffer_57
  Comparator comparator_64 (.a(8'hf6), .b(data_pass), .eq(comparator_64_eq));  // open: gt, lt
  assign data_pass_translated_down = comparator_64_eq ? 32'h400000 : 32'bz;  // Controlled_Buffer controlled_buffer_58
  Comparator comparator_65 (.a(8'hf7), .b(data_pass), .eq(comparator_65_eq));  // open: gt, lt
  assign data_pass_translated_down = comparator_65_eq ? 32'h800000 : 32'bz;  // Controlled_Buffer controlled_buffer_59
  Comparator comparator_66 (.a(8'hf8), .b(data_pass), .eq(comparator_66_eq));  // open: gt, lt
  assign data_pass_translated_down = comparator_66_eq ? 32'h1000000 : 32'bz;  // Controlled_Buffer controlled_buffer_60
  Comparator comparator_67 (.a(8'hf9), .b(data_pass), .eq(comparator_67_eq));  // open: gt, lt
  assign data_pass_translated_down = comparator_67_eq ? 32'h2000000 : 32'bz;  // Controlled_Buffer controlled_buffer_61
  Comparator comparator_68 (.a(8'hfa), .b(data_pass), .eq(comparator_68_eq));  // open: gt, lt
  assign data_pass_translated_down = comparator_68_eq ? 32'h4000000 : 32'bz;  // Controlled_Buffer controlled_buffer_62
  Comparator comparator_69 (.a(8'hfb), .b(data_pass), .eq(comparator_69_eq));  // open: gt, lt
  assign data_pass_translated_down = comparator_69_eq ? 32'h8000000 : 32'bz;  // Controlled_Buffer controlled_buffer_63
  Comparator comparator_70 (.a(8'hfc), .b(data_pass), .eq(comparator_70_eq));  // open: gt, lt
  assign data_pass_translated_down = comparator_70_eq ? 32'h10000000 : 32'bz;  // Controlled_Buffer controlled_buffer_64
  Comparator comparator_71 (.a(8'hfd), .b(data_pass), .eq(comparator_71_eq));  // open: gt, lt
  assign data_pass_translated_down = comparator_71_eq ? 32'h20000000 : 32'bz;  // Controlled_Buffer controlled_buffer_65
  Comparator comparator_72 (.a(8'hfe), .b(data_pass), .eq(comparator_72_eq));  // open: gt, lt
  assign data_pass_translated_down = comparator_72_eq ? 32'h40000000 : 32'bz;  // Controlled_Buffer controlled_buffer_66
  Comparator comparator_73 (.a({8{1'b1}}), .b(data_pass), .eq(comparator_73_eq));  // open: gt, lt
  assign data_pass_translated_down = comparator_73_eq ? 32'h80000000 : 32'bz;  // Controlled_Buffer controlled_buffer_67
  // Probe on x_counter
  Comparator comparator_74 (.a(x_counter), .b({8{1'b0}}), .eq(trig_32));  // open: gt, lt
  Comparator comparator_75 (.a(x_counter), .b(8'h1), .eq(trig_31));  // open: gt, lt
  Comparator comparator_76 (.a(x_counter), .b(8'h2), .eq(trig_30));  // open: gt, lt
  Comparator comparator_77 (.a(x_counter), .b(8'h3), .eq(trig_29));  // open: gt, lt
  Comparator comparator_78 (.a(x_counter), .b(8'h4), .eq(trig_28));  // open: gt, lt
  Comparator comparator_79 (.a(x_counter), .b(8'h5), .eq(trig_27));  // open: gt, lt
  Comparator comparator_80 (.a(x_counter), .b(8'h6), .eq(trig_26));  // open: gt, lt
  Comparator comparator_81 (.a(x_counter), .b(8'h7), .eq(trig_25));  // open: gt, lt
  Comparator comparator_82 (.a(x_counter), .b(8'h8), .eq(trig_24));  // open: gt, lt
  Comparator comparator_83 (.a(x_counter), .b(8'h9), .eq(trig_23));  // open: gt, lt
  Comparator comparator_84 (.a(x_counter), .b(8'ha), .eq(trig_22));  // open: gt, lt
  Comparator comparator_85 (.a(x_counter), .b(8'hb), .eq(trig_21));  // open: gt, lt
  Comparator comparator_86 (.a(x_counter), .b(8'hc), .eq(trig_20));  // open: gt, lt
  Comparator comparator_87 (.a(x_counter), .b(8'hd), .eq(trig_19));  // open: gt, lt
  Comparator comparator_88 (.a(x_counter), .b(8'hf), .eq(trig_18));  // open: gt, lt
  Comparator comparator_89 (.a(x_counter), .b(8'h10), .eq(trig_17));  // open: gt, lt
  Comparator comparator_90 (.a(x_counter), .b(8'h11), .eq(trig_16));  // open: gt, lt
  Comparator comparator_91 (.a(x_counter), .b(8'h12), .eq(trig_15));  // open: gt, lt
  Comparator comparator_92 (.a(x_counter), .b(8'h13), .eq(trig_14));  // open: gt, lt
  Comparator comparator_93 (.a(x_counter), .b(8'h14), .eq(trig_13));  // open: gt, lt
  Comparator comparator_94 (.a(x_counter), .b(8'h15), .eq(trig_12));  // open: gt, lt
  Comparator comparator_95 (.a(x_counter), .b(8'h16), .eq(trig_11));  // open: gt, lt
  Comparator comparator_96 (.a(x_counter), .b(8'h17), .eq(trig_10));  // open: gt, lt
  Comparator comparator_97 (.a(x_counter), .b(8'h18), .eq(trig_9));  // open: gt, lt
  Comparator comparator_98 (.a(x_counter), .b(8'h19), .eq(trig_8));  // open: gt, lt
  Comparator comparator_99 (.a(x_counter), .b(8'h1a), .eq(trig_7));  // open: gt, lt
  Comparator comparator_100 (.a(x_counter), .b(8'h1b), .eq(trig_6));  // open: gt, lt
  Comparator comparator_101 (.a(x_counter), .b(8'h1c), .eq(trig_5));  // open: gt, lt
  Comparator comparator_102 (.a(x_counter), .b(8'h1d), .eq(trig_4));  // open: gt, lt
  Comparator comparator_103 (.a(x_counter), .b(8'h1e), .eq(trig_3));  // open: gt, lt
  Comparator comparator_104 (.a(x_counter), .b(8'h1f), .eq(trig_2));  // open: gt, lt
  Comparator comparator_105 (.a(x_counter), .b(8'h20), .eq(trig_1));  // open: gt, lt
  // Probe on x_counter
  Comparator comparator_106 (.a(x_counter), .b(8'h21), .eq(trig_2_1));  // open: gt, lt
  Comparator comparator_107 (.a(x_counter), .b(8'h22), .eq(trig_2_2));  // open: gt, lt
  Comparator comparator_108 (.a(x_counter), .b(8'h23), .eq(trig_2_3));  // open: gt, lt
  Comparator comparator_109 (.a(x_counter), .b(8'h24), .eq(trig_2_4));  // open: gt, lt
  Comparator comparator_110 (.a(x_counter), .b(8'h25), .eq(trig_2_5));  // open: gt, lt
  Comparator comparator_111 (.a(x_counter), .b(8'h26), .eq(trig_2_6));  // open: gt, lt
  Comparator comparator_112 (.a(x_counter), .b(8'h27), .eq(trig_2_7));  // open: gt, lt
  Comparator comparator_113 (.a(x_counter), .b(8'h28), .eq(trig_2_8));  // open: gt, lt
  Comparator comparator_114 (.a(x_counter), .b(8'h29), .eq(trig_2_9));  // open: gt, lt
  Comparator comparator_115 (.a(x_counter), .b(8'h2a), .eq(trig_2_10));  // open: gt, lt
  Comparator comparator_116 (.a(x_counter), .b(8'h2b), .eq(trig_2_11));  // open: gt, lt
  Comparator comparator_117 (.a(x_counter), .b(8'h2c), .eq(trig_2_12));  // open: gt, lt
  Comparator comparator_118 (.a(x_counter), .b(8'h2d), .eq(trig_2_13));  // open: gt, lt
  Comparator comparator_119 (.a(x_counter), .b(8'h2e), .eq(trig_2_14));  // open: gt, lt
  Comparator comparator_120 (.a(x_counter), .b(8'h2f), .eq(trig_2_15));  // open: gt, lt
  Comparator comparator_121 (.a(x_counter), .b(8'h30), .eq(trig_2_16));  // open: gt, lt
  Comparator comparator_122 (.a(x_counter), .b(8'h31), .eq(trig_2_17));  // open: gt, lt
  Comparator comparator_123 (.a(x_counter), .b(8'h32), .eq(trig_2_18));  // open: gt, lt
  Comparator comparator_124 (.a(x_counter), .b(8'h33), .eq(trig_2_19));  // open: gt, lt
  Comparator comparator_125 (.a(x_counter), .b(8'h34), .eq(trig_2_20));  // open: gt, lt
  Comparator comparator_126 (.a(x_counter), .b(8'h35), .eq(trig_2_21));  // open: gt, lt
  Comparator comparator_127 (.a(x_counter), .b(8'h36), .eq(trig_2_22));  // open: gt, lt
  Comparator comparator_128 (.a(x_counter), .b(8'h37), .eq(trig_2_23));  // open: gt, lt
  Comparator comparator_129 (.a(x_counter), .b(8'h38), .eq(trig_2_24));  // open: gt, lt
  Comparator comparator_130 (.a(x_counter), .b(8'h39), .eq(trig_2_25));  // open: gt, lt
  Comparator comparator_131 (.a(x_counter), .b(8'h3a), .eq(trig_2_26));  // open: gt, lt
  Comparator comparator_132 (.a(x_counter), .b(8'h3b), .eq(trig_2_27));  // open: gt, lt
  Comparator comparator_133 (.a(x_counter), .b(8'h3c), .eq(trig_2_28));  // open: gt, lt
  Comparator comparator_134 (.a(x_counter), .b(8'h3d), .eq(trig_2_29));  // open: gt, lt
  Comparator comparator_135 (.a(x_counter), .b(8'h3e), .eq(trig_2_30));  // open: gt, lt
  Comparator comparator_136 (.a(x_counter), .b(8'h3f), .eq(trig_2_31));  // open: gt, lt
  Comparator comparator_137 (.a(x_counter), .b(8'h40), .eq(trig_2_32));  // open: gt, lt
  Multiplexer #(.width(32), .enable("false")) multiplexer_9 (
    .in0(data_pass_translated_up), .in1({32{1'b0}}), .out(multiplexer_9_out), .sel(data_pass[7]));
  Multiplexer #(.width(32), .enable("false")) multiplexer_10 (
    .in0({32{1'b0}}), .in1(data_pass_translated_down), .out(multiplexer_10_out), .sel(data_pass[7]));
  Multiplexer #(.width(32), .enable("false")) multiplexer_11 (
    .in0(data_pass_translated_up), .in1({32{1'b0}}), .out(multiplexer_11_out), .sel(data_pass[7]));
  Multiplexer #(.width(32), .enable("false")) multiplexer_12 (
    .in0({32{1'b0}}), .in1(data_pass_translated_down), .out(multiplexer_12_out), .sel(data_pass[7]));
  Multiplexer #(.width(32), .enable("false")) multiplexer_13 (
    .in0(data_pass_translated_up), .in1({32{1'b0}}), .out(multiplexer_13_out), .sel(data_pass[7]));
  Multiplexer #(.width(32), .enable("false")) multiplexer_14 (
    .in0({32{1'b0}}), .in1(data_pass_translated_down), .out(multiplexer_14_out), .sel(data_pass[7]));
  Multiplexer #(.width(32), .enable("false")) multiplexer_15 (
    .in0(data_pass_translated_up), .in1({32{1'b0}}), .out(multiplexer_15_out), .sel(data_pass[7]));
  Multiplexer #(.width(32), .enable("false")) multiplexer_16 (
    .in0({32{1'b0}}), .in1(data_pass_translated_down), .out(multiplexer_16_out), .sel(data_pass[7]));
  Multiplexer #(.width(32), .enable("false")) multiplexer_17 (
    .in0(data_pass_translated_up), .in1({32{1'b0}}), .out(multiplexer_17_out), .sel(data_pass[7]));
  Multiplexer #(.width(32), .enable("false")) multiplexer_18 (
    .in0({32{1'b0}}), .in1(data_pass_translated_down), .out(multiplexer_18_out), .sel(data_pass[7]));
  Multiplexer #(.width(32), .enable("false")) multiplexer_19 (
    .in0(data_pass_translated_up), .in1({32{1'b0}}), .out(multiplexer_19_out), .sel(data_pass[7]));
  Multiplexer #(.width(32), .enable("false")) multiplexer_20 (
    .in0({32{1'b0}}), .in1(data_pass_translated_down), .out(multiplexer_20_out), .sel(data_pass[7]));
  Multiplexer #(.width(32), .enable("false")) multiplexer_21 (
    .in0(data_pass_translated_up), .in1({32{1'b0}}), .out(multiplexer_21_out), .sel(data_pass[7]));
  Multiplexer #(.width(32), .enable("false")) multiplexer_22 (
    .in0({32{1'b0}}), .in1(data_pass_translated_down), .out(multiplexer_22_out), .sel(data_pass[7]));
  Multiplexer #(.width(32), .enable("false")) multiplexer_23 (
    .in0(data_pass_translated_up), .in1({32{1'b0}}), .out(multiplexer_23_out), .sel(data_pass[7]));
  Multiplexer #(.width(32), .enable("false")) multiplexer_24 (
    .in0({32{1'b0}}), .in1(data_pass_translated_down), .out(multiplexer_24_out), .sel(data_pass[7]));
  Multiplexer #(.width(32), .enable("false")) multiplexer_25 (
    .in0(data_pass_translated_up), .in1({32{1'b0}}), .out(multiplexer_25_out), .sel(data_pass[7]));
  Multiplexer #(.width(32), .enable("false")) multiplexer_26 (
    .in0({32{1'b0}}), .in1(data_pass_translated_down), .out(multiplexer_26_out), .sel(data_pass[7]));
  Multiplexer #(.width(32), .enable("false")) multiplexer_27 (
    .in0(data_pass_translated_up), .in1({32{1'b0}}), .out(multiplexer_27_out), .sel(data_pass[7]));
  Multiplexer #(.width(32), .enable("false")) multiplexer_28 (
    .in0({32{1'b0}}), .in1(data_pass_translated_down), .out(multiplexer_28_out), .sel(data_pass[7]));
  Multiplexer #(.width(32), .enable("false")) multiplexer_29 (
    .in0(data_pass_translated_up), .in1({32{1'b0}}), .out(multiplexer_29_out), .sel(data_pass[7]));
  Multiplexer #(.width(32), .enable("false")) multiplexer_30 (
    .in0({32{1'b0}}), .in1(data_pass_translated_down), .out(multiplexer_30_out), .sel(data_pass[7]));
  Multiplexer #(.width(32), .enable("false")) multiplexer_31 (
    .in0(data_pass_translated_up), .in1({32{1'b0}}), .out(multiplexer_31_out), .sel(data_pass[7]));
  Multiplexer #(.width(32), .enable("false")) multiplexer_32 (
    .in0({32{1'b0}}), .in1(data_pass_translated_down), .out(multiplexer_32_out), .sel(data_pass[7]));
  Multiplexer #(.width(32), .enable("false")) multiplexer_33 (
    .in0(data_pass_translated_up), .in1({32{1'b0}}), .out(multiplexer_33_out), .sel(data_pass[7]));
  Multiplexer #(.width(32), .enable("false")) multiplexer_34 (
    .in0({32{1'b0}}), .in1(data_pass_translated_down), .out(multiplexer_34_out), .sel(data_pass[7]));
  Multiplexer #(.width(32), .enable("false")) multiplexer_35 (
    .in0(data_pass_translated_up), .in1({32{1'b0}}), .out(multiplexer_35_out), .sel(data_pass[7]));
  Multiplexer #(.width(32), .enable("false")) multiplexer_36 (
    .in0({32{1'b0}}), .in1(data_pass_translated_down), .out(multiplexer_36_out), .sel(data_pass[7]));
  Multiplexer #(.width(32), .enable("false")) multiplexer_37 (
    .in0(data_pass_translated_up), .in1({32{1'b0}}), .out(multiplexer_37_out), .sel(data_pass[7]));
  Multiplexer #(.width(32), .enable("false")) multiplexer_38 (
    .in0({32{1'b0}}), .in1(data_pass_translated_down), .out(multiplexer_38_out), .sel(data_pass[7]));
  Multiplexer #(.width(32), .enable("false")) multiplexer_39 (
    .in0(data_pass_translated_up), .in1({32{1'b0}}), .out(multiplexer_39_out), .sel(data_pass[7]));
  Multiplexer #(.width(32), .enable("false")) multiplexer_40 (
    .in0({32{1'b0}}), .in1(data_pass_translated_down), .out(multiplexer_40_out), .sel(data_pass[7]));
  Multiplexer #(.width(32), .enable("false")) multiplexer_41 (
    .in0(data_pass_translated_up), .in1({32{1'b0}}), .out(multiplexer_41_out), .sel(data_pass[7]));
  Multiplexer #(.width(32), .enable("false")) multiplexer_42 (
    .in0({32{1'b0}}), .in1(data_pass_translated_down), .out(multiplexer_42_out), .sel(data_pass[7]));
  // Probe on multiplexer_9_out
  // Probe on multiplexer_10_out
  // Probe on multiplexer_11_out
  // Probe on multiplexer_12_out
  // Probe on multiplexer_13_out
  // Probe on multiplexer_14_out
  // Probe on multiplexer_15_out
  // Probe on multiplexer_16_out
  // Probe on multiplexer_17_out
  // Probe on multiplexer_18_out
  // Probe on multiplexer_19_out
  // Probe on multiplexer_20_out
  // Probe on multiplexer_21_out
  // Probe on multiplexer_22_out
  // Probe on multiplexer_23_out
  // Probe on multiplexer_24_out
  // Probe on multiplexer_25_out
  // Probe on multiplexer_26_out
  // Probe on multiplexer_27_out
  // Probe on multiplexer_28_out
  // Probe on multiplexer_29_out
  // Probe on multiplexer_30_out
  // Probe on multiplexer_31_out
  // Probe on multiplexer_32_out
  // Probe on multiplexer_33_out
  // Probe on multiplexer_34_out
  // Probe on multiplexer_35_out
  // Probe on multiplexer_36_out
  // Probe on multiplexer_37_out
  // Probe on multiplexer_38_out
  // Probe on multiplexer_39_out
  // Probe on multiplexer_40_out
  // Probe on multiplexer_41_out
  // Probe on multiplexer_42_out
  Register #(.width(32)) register_9 (.D(multiplexer_9_out), .en(trig_32), .Q(led1_32), .clk(trig_32));  // open: clr
  Register #(.width(32)) register_10 (.D(multiplexer_11_out), .en(trig_31), .Q(led1_31), .clk(trig_31));  // open: clr
  Register #(.width(32)) register_11 (.D(multiplexer_13_out), .en(trig_30), .Q(led1_30), .clk(trig_30));  // open: clr
  Register #(.width(32)) register_12 (.D(multiplexer_15_out), .en(trig_29), .Q(led1_29), .clk(trig_29));  // open: clr
  Register #(.width(32)) register_13 (.D(multiplexer_17_out), .en(trig_28), .Q(led1_28), .clk(trig_28));  // open: clr
  Register #(.width(32)) register_14 (.D(multiplexer_19_out), .en(trig_27), .Q(led1_27), .clk(trig_27));  // open: clr
  Register #(.width(32)) register_15 (.D(multiplexer_21_out), .en(trig_26), .Q(led1_26), .clk(trig_26));  // open: clr
  Register #(.width(32)) register_16 (.D(multiplexer_23_out), .en(trig_25), .Q(led1_25), .clk(trig_25));  // open: clr
  Register #(.width(32)) register_17 (.D(multiplexer_25_out), .en(trig_24), .Q(led1_24), .clk(trig_24));  // open: clr
  Register #(.width(32)) register_18 (.D(multiplexer_27_out), .en(trig_23), .Q(led1_23), .clk(trig_23));  // open: clr
  Register #(.width(32)) register_19 (.D(multiplexer_29_out), .en(trig_22), .Q(led1_22), .clk(trig_22));  // open: clr
  Register #(.width(32)) register_20 (.D(multiplexer_31_out), .en(trig_21), .Q(led1_21), .clk(trig_21));  // open: clr
  Register #(.width(32)) register_21 (.D(multiplexer_33_out), .en(trig_20), .Q(led1_20), .clk(trig_20));  // open: clr
  Register #(.width(32)) register_22 (.D(multiplexer_35_out), .en(trig_19), .Q(led1_19), .clk(trig_19));  // open: clr
  Register #(.width(32)) register_23 (.D(multiplexer_37_out), .en(trig_18), .Q(led1_18), .clk(trig_18));  // open: clr
  Register #(.width(32)) register_24 (.D(multiplexer_39_out), .en(trig_17), .Q(led1_17), .clk(trig_17));  // open: clr
  Register #(.width(32)) register_25 (.D(multiplexer_41_out), .en(trig_16), .Q(led1_16), .clk(trig_16));  // open: clr
  Register #(.width(32)) register_26 (.D(multiplexer_10_out), .en(trig_32), .Q(led2_32), .clk(trig_32));  // open: clr
  Register #(.width(32)) register_27 (.D(multiplexer_12_out), .en(trig_31), .Q(led2_31), .clk(trig_31));  // open: clr
  Register #(.width(32)) register_28 (.D(multiplexer_14_out), .en(trig_30), .Q(led2_30), .clk(trig_30));  // open: clr
  Register #(.width(32)) register_29 (.D(multiplexer_16_out), .en(trig_29), .Q(led2_29), .clk(trig_29));  // open: clr
  Register #(.width(32)) register_30 (.D(multiplexer_18_out), .en(trig_28), .Q(led2_28), .clk(trig_28));  // open: clr
  Register #(.width(32)) register_31 (.D(multiplexer_20_out), .en(trig_27), .Q(led2_27), .clk(trig_27));  // open: clr
  Register #(.width(32)) register_32 (.D(multiplexer_22_out), .en(trig_26), .Q(led2_26), .clk(trig_26));  // open: clr
  Register #(.width(32)) register_33 (.D(multiplexer_24_out), .en(trig_25), .Q(led2_25), .clk(trig_25));  // open: clr
  Register #(.width(32)) register_34 (.D(multiplexer_26_out), .en(trig_24), .Q(led2_24), .clk(trig_24));  // open: clr
  Register #(.width(32)) register_35 (.D(multiplexer_28_out), .en(trig_23), .Q(led2_23), .clk(trig_23));  // open: clr
  Register #(.width(32)) register_36 (.D(multiplexer_30_out), .en(trig_22), .Q(led2_22), .clk(trig_22));  // open: clr
  Register #(.width(32)) register_37 (.D(multiplexer_32_out), .en(trig_21), .Q(led2_21), .clk(trig_21));  // open: clr
  Register #(.width(32)) register_38 (.D(multiplexer_34_out), .en(trig_20), .Q(led2_20), .clk(trig_20));  // open: clr
  Register #(.width(32)) register_39 (.D(multiplexer_36_out), .en(trig_19), .Q(led2_19), .clk(trig_19));  // open: clr
  Register #(.width(32)) register_40 (.D(multiplexer_38_out), .en(trig_18), .Q(led2_18), .clk(trig_18));  // open: clr
  Register #(.width(32)) register_41 (.D(multiplexer_40_out), .en(trig_17), .Q(led2_17), .clk(trig_17));  // open: clr
  Register #(.width(32)) register_42 (.D(multiplexer_42_out), .en(trig_16), .Q(led2_16), .clk(trig_16));  // open: clr
  // Probe on multiplexer_43_out
  Multiplexer #(.width(32), .enable("false")) multiplexer_43 (
    .in0(data_pass_translated_up), .in1({32{1'b0}}), .out(multiplexer_43_out), .sel(data_pass[7]));
  // Probe on multiplexer_44_out
  Multiplexer #(.width(32), .enable("false")) multiplexer_44 (
    .in0({32{1'b0}}), .in1(data_pass_translated_down), .out(multiplexer_44_out), .sel(data_pass[7]));
  // Probe on multiplexer_45_out
  Multiplexer #(.width(32), .enable("false")) multiplexer_45 (
    .in0(data_pass_translated_up), .in1({32{1'b0}}), .out(multiplexer_45_out), .sel(data_pass[7]));
  // Probe on multiplexer_46_out
  Multiplexer #(.width(32), .enable("false")) multiplexer_46 (
    .in0({32{1'b0}}), .in1(data_pass_translated_down), .out(multiplexer_46_out), .sel(data_pass[7]));
  // Probe on multiplexer_47_out
  Multiplexer #(.width(32), .enable("false")) multiplexer_47 (
    .in0(data_pass_translated_up), .in1({32{1'b0}}), .out(multiplexer_47_out), .sel(data_pass[7]));
  // Probe on multiplexer_48_out
  Multiplexer #(.width(32), .enable("false")) multiplexer_48 (
    .in0({32{1'b0}}), .in1(data_pass_translated_down), .out(multiplexer_48_out), .sel(data_pass[7]));
  // Probe on multiplexer_49_out
  Multiplexer #(.width(32), .enable("false")) multiplexer_49 (
    .in0(data_pass_translated_up), .in1({32{1'b0}}), .out(multiplexer_49_out), .sel(data_pass[7]));
  // Probe on multiplexer_50_out
  Multiplexer #(.width(32), .enable("false")) multiplexer_50 (
    .in0({32{1'b0}}), .in1(data_pass_translated_down), .out(multiplexer_50_out), .sel(data_pass[7]));
  // Probe on multiplexer_51_out
  Multiplexer #(.width(32), .enable("false")) multiplexer_51 (
    .in0(data_pass_translated_up), .in1({32{1'b0}}), .out(multiplexer_51_out), .sel(data_pass[7]));
  // Probe on multiplexer_52_out
  Multiplexer #(.width(32), .enable("false")) multiplexer_52 (
    .in0({32{1'b0}}), .in1(data_pass_translated_down), .out(multiplexer_52_out), .sel(data_pass[7]));
  // Probe on multiplexer_53_out
  Multiplexer #(.width(32), .enable("false")) multiplexer_53 (
    .in0(data_pass_translated_up), .in1({32{1'b0}}), .out(multiplexer_53_out), .sel(data_pass[7]));
  // Probe on multiplexer_54_out
  Multiplexer #(.width(32), .enable("false")) multiplexer_54 (
    .in0({32{1'b0}}), .in1(data_pass_translated_down), .out(multiplexer_54_out), .sel(data_pass[7]));
  // Probe on multiplexer_55_out
  Multiplexer #(.width(32), .enable("false")) multiplexer_55 (
    .in0(data_pass_translated_up), .in1({32{1'b0}}), .out(multiplexer_55_out), .sel(data_pass[7]));
  // Probe on multiplexer_56_out
  Multiplexer #(.width(32), .enable("false")) multiplexer_56 (
    .in0({32{1'b0}}), .in1(data_pass_translated_down), .out(multiplexer_56_out), .sel(data_pass[7]));
  // Probe on multiplexer_57_out
  Multiplexer #(.width(32), .enable("false")) multiplexer_57 (
    .in0(data_pass_translated_up), .in1({32{1'b0}}), .out(multiplexer_57_out), .sel(data_pass[7]));
  // Probe on multiplexer_58_out
  Multiplexer #(.width(32), .enable("false")) multiplexer_58 (
    .in0({32{1'b0}}), .in1(data_pass_translated_down), .out(multiplexer_58_out), .sel(data_pass[7]));
  // Probe on multiplexer_59_out
  Multiplexer #(.width(32), .enable("false")) multiplexer_59 (
    .in0(data_pass_translated_up), .in1({32{1'b0}}), .out(multiplexer_59_out), .sel(data_pass[7]));
  // Probe on multiplexer_60_out
  Multiplexer #(.width(32), .enable("false")) multiplexer_60 (
    .in0({32{1'b0}}), .in1(data_pass_translated_down), .out(multiplexer_60_out), .sel(data_pass[7]));
  // Probe on multiplexer_61_out
  Multiplexer #(.width(32), .enable("false")) multiplexer_61 (
    .in0(data_pass_translated_up), .in1({32{1'b0}}), .out(multiplexer_61_out), .sel(data_pass[7]));
  // Probe on multiplexer_62_out
  Multiplexer #(.width(32), .enable("false")) multiplexer_62 (
    .in0({32{1'b0}}), .in1(data_pass_translated_down), .out(multiplexer_62_out), .sel(data_pass[7]));
  // Probe on multiplexer_63_out
  Multiplexer #(.width(32), .enable("false")) multiplexer_63 (
    .in0(data_pass_translated_up), .in1({32{1'b0}}), .out(multiplexer_63_out), .sel(data_pass[7]));
  // Probe on multiplexer_64_out
  Multiplexer #(.width(32), .enable("false")) multiplexer_64 (
    .in0({32{1'b0}}), .in1(data_pass_translated_down), .out(multiplexer_64_out), .sel(data_pass[7]));
  // Probe on multiplexer_65_out
  Multiplexer #(.width(32), .enable("false")) multiplexer_65 (
    .in0(data_pass_translated_up), .in1({32{1'b0}}), .out(multiplexer_65_out), .sel(data_pass[7]));
  // Probe on multiplexer_66_out
  Multiplexer #(.width(32), .enable("false")) multiplexer_66 (
    .in0({32{1'b0}}), .in1(data_pass_translated_down), .out(multiplexer_66_out), .sel(data_pass[7]));
  // Probe on multiplexer_67_out
  Multiplexer #(.width(32), .enable("false")) multiplexer_67 (
    .in0(data_pass_translated_up), .in1({32{1'b0}}), .out(multiplexer_67_out), .sel(data_pass[7]));
  // Probe on multiplexer_68_out
  Multiplexer #(.width(32), .enable("false")) multiplexer_68 (
    .in0({32{1'b0}}), .in1(data_pass_translated_down), .out(multiplexer_68_out), .sel(data_pass[7]));
  // Probe on multiplexer_69_out
  Multiplexer #(.width(32), .enable("false")) multiplexer_69 (
    .in0(data_pass_translated_up), .in1({32{1'b0}}), .out(multiplexer_69_out), .sel(data_pass[7]));
  // Probe on multiplexer_70_out
  Multiplexer #(.width(32), .enable("false")) multiplexer_70 (
    .in0({32{1'b0}}), .in1(data_pass_translated_down), .out(multiplexer_70_out), .sel(data_pass[7]));
  // Probe on multiplexer_71_out
  Multiplexer #(.width(32), .enable("false")) multiplexer_71 (
    .in0(data_pass_translated_up), .in1({32{1'b0}}), .out(multiplexer_71_out), .sel(data_pass[7]));
  // Probe on multiplexer_72_out
  Multiplexer #(.width(32), .enable("false")) multiplexer_72 (
    .in0({32{1'b0}}), .in1(data_pass_translated_down), .out(multiplexer_72_out), .sel(data_pass[7]));
  Register #(.width(32)) register_43 (.D(multiplexer_43_out), .en(trig_15), .Q(led1_15), .clk(trig_15));  // open: clr
  Register #(.width(32)) register_44 (.D(multiplexer_44_out), .en(trig_15), .Q(led2_15), .clk(trig_15));  // open: clr
  Register #(.width(32)) register_45 (.D(multiplexer_45_out), .en(trig_14), .Q(led1_14), .clk(trig_14));  // open: clr
  Register #(.width(32)) register_46 (.D(multiplexer_46_out), .en(trig_14), .Q(led2_14), .clk(trig_14));  // open: clr
  Register #(.width(32)) register_47 (.D(multiplexer_47_out), .en(trig_13), .Q(led1_13), .clk(trig_13));  // open: clr
  Register #(.width(32)) register_48 (.D(multiplexer_48_out), .en(trig_13), .Q(led2_13), .clk(trig_13));  // open: clr
  Register #(.width(32)) register_49 (.D(multiplexer_49_out), .en(trig_12), .Q(led1_12), .clk(trig_12));  // open: clr
  Register #(.width(32)) register_50 (.D(multiplexer_50_out), .en(trig_12), .Q(led2_12), .clk(trig_12));  // open: clr
  Register #(.width(32)) register_51 (.D(multiplexer_51_out), .en(trig_11), .Q(led1_11), .clk(trig_11));  // open: clr
  Register #(.width(32)) register_52 (.D(multiplexer_52_out), .en(trig_11), .Q(led2_11), .clk(trig_11));  // open: clr
  Register #(.width(32)) register_53 (.D(multiplexer_53_out), .en(trig_10), .Q(led1_10), .clk(trig_10));  // open: clr
  Register #(.width(32)) register_54 (.D(multiplexer_54_out), .en(trig_10), .Q(led2_10), .clk(trig_10));  // open: clr
  Register #(.width(32)) register_55 (.D(multiplexer_55_out), .en(trig_9), .Q(led1_9), .clk(trig_9));  // open: clr
  Register #(.width(32)) register_56 (.D(multiplexer_56_out), .en(trig_9), .Q(led2_9), .clk(trig_9));  // open: clr
  Register #(.width(32)) register_57 (.D(multiplexer_57_out), .en(trig_8), .Q(led1_8), .clk(trig_8));  // open: clr
  Register #(.width(32)) register_58 (.D(multiplexer_58_out), .en(trig_8), .Q(led2_8), .clk(trig_8));  // open: clr
  Register #(.width(32)) register_59 (.D(multiplexer_59_out), .en(trig_7), .Q(led1_7), .clk(trig_7));  // open: clr
  Register #(.width(32)) register_60 (.D(multiplexer_60_out), .en(trig_7), .Q(led2_7), .clk(trig_7));  // open: clr
  Register #(.width(32)) register_61 (.D(multiplexer_61_out), .en(trig_6), .Q(led1_6), .clk(trig_6));  // open: clr
  Register #(.width(32)) register_62 (.D(multiplexer_62_out), .en(trig_6), .Q(led2_6), .clk(trig_6));  // open: clr
  Register #(.width(32)) register_63 (.D(multiplexer_63_out), .en(trig_5), .Q(led1_5), .clk(trig_5));  // open: clr
  Register #(.width(32)) register_64 (.D(multiplexer_64_out), .en(trig_5), .Q(led2_5), .clk(trig_5));  // open: clr
  Register #(.width(32)) register_65 (.D(multiplexer_65_out), .en(trig_4), .Q(led1_4), .clk(trig_4));  // open: clr
  Register #(.width(32)) register_66 (.D(multiplexer_66_out), .en(trig_4), .Q(led2_4), .clk(trig_4));  // open: clr
  Register #(.width(32)) register_67 (.D(multiplexer_67_out), .en(trig_3), .Q(led1_3), .clk(trig_3));  // open: clr
  Register #(.width(32)) register_68 (.D(multiplexer_68_out), .en(trig_3), .Q(led2_3), .clk(trig_3));  // open: clr
  Register #(.width(32)) register_69 (.D(multiplexer_69_out), .en(trig_2), .Q(led1_2), .clk(trig_2));  // open: clr
  Register #(.width(32)) register_70 (.D(multiplexer_70_out), .en(trig_2), .Q(led2_2), .clk(trig_2));  // open: clr
  Register #(.width(32)) register_71 (.D(multiplexer_71_out), .en(trig_1), .Q(led1_1), .clk(trig_1), .clr(trig_1));
  Register #(.width(32)) register_72 (.D(multiplexer_72_out), .en(trig_1), .Q(led2_1), .clk(trig_1));  // open: clr
  Multiplexer #(.width(32), .enable("false")) multiplexer_73 (
    .in0(data_pass_translated_up), .in1({32{1'b0}}), .out(multiplexer_73_out), .sel(data_pass[7]));
  Multiplexer #(.width(32), .enable("false")) multiplexer_74 (
    .in0({32{1'b0}}), .in1(data_pass_translated_down), .out(multiplexer_74_out), .sel(data_pass[7]));
  Multiplexer #(.width(32), .enable("false")) multiplexer_75 (
    .in0(data_pass_translated_up), .in1({32{1'b0}}), .out(multiplexer_75_out), .sel(data_pass[7]));
  Multiplexer #(.width(32), .enable("false")) multiplexer_76 (
    .in0({32{1'b0}}), .in1(data_pass_translated_down), .out(multiplexer_76_out), .sel(data_pass[7]));
  Multiplexer #(.width(32), .enable("false")) multiplexer_77 (
    .in0(data_pass_translated_up), .in1({32{1'b0}}), .out(multiplexer_77_out), .sel(data_pass[7]));
  Multiplexer #(.width(32), .enable("false")) multiplexer_78 (
    .in0({32{1'b0}}), .in1(data_pass_translated_down), .out(multiplexer_78_out), .sel(data_pass[7]));
  Multiplexer #(.width(32), .enable("false")) multiplexer_79 (
    .in0(data_pass_translated_up), .in1({32{1'b0}}), .out(multiplexer_79_out), .sel(data_pass[7]));
  Multiplexer #(.width(32), .enable("false")) multiplexer_80 (
    .in0({32{1'b0}}), .in1(data_pass_translated_down), .out(multiplexer_80_out), .sel(data_pass[7]));
  Multiplexer #(.width(32), .enable("false")) multiplexer_81 (
    .in0(data_pass_translated_up), .in1({32{1'b0}}), .out(multiplexer_81_out), .sel(data_pass[7]));
  Multiplexer #(.width(32), .enable("false")) multiplexer_82 (
    .in0({32{1'b0}}), .in1(data_pass_translated_down), .out(multiplexer_82_out), .sel(data_pass[7]));
  Multiplexer #(.width(32), .enable("false")) multiplexer_83 (
    .in0(data_pass_translated_up), .in1({32{1'b0}}), .out(multiplexer_83_out), .sel(data_pass[7]));
  Multiplexer #(.width(32), .enable("false")) multiplexer_84 (
    .in0({32{1'b0}}), .in1(data_pass_translated_down), .out(multiplexer_84_out), .sel(data_pass[7]));
  Multiplexer #(.width(32), .enable("false")) multiplexer_85 (
    .in0(data_pass_translated_up), .in1({32{1'b0}}), .out(multiplexer_85_out), .sel(data_pass[7]));
  Multiplexer #(.width(32), .enable("false")) multiplexer_86 (
    .in0({32{1'b0}}), .in1(data_pass_translated_down), .out(multiplexer_86_out), .sel(data_pass[7]));
  Multiplexer #(.width(32), .enable("false")) multiplexer_87 (
    .in0(data_pass_translated_up), .in1({32{1'b0}}), .out(multiplexer_87_out), .sel(data_pass[7]));
  Multiplexer #(.width(32), .enable("false")) multiplexer_88 (
    .in0({32{1'b0}}), .in1(data_pass_translated_down), .out(multiplexer_88_out), .sel(data_pass[7]));
  Multiplexer #(.width(32), .enable("false")) multiplexer_89 (
    .in0(data_pass_translated_up), .in1({32{1'b0}}), .out(multiplexer_89_out), .sel(data_pass[7]));
  Multiplexer #(.width(32), .enable("false")) multiplexer_90 (
    .in0({32{1'b0}}), .in1(data_pass_translated_down), .out(multiplexer_90_out), .sel(data_pass[7]));
  Multiplexer #(.width(32), .enable("false")) multiplexer_91 (
    .in0(data_pass_translated_up), .in1({32{1'b0}}), .out(multiplexer_91_out), .sel(data_pass[7]));
  Multiplexer #(.width(32), .enable("false")) multiplexer_92 (
    .in0({32{1'b0}}), .in1(data_pass_translated_down), .out(multiplexer_92_out), .sel(data_pass[7]));
  Multiplexer #(.width(32), .enable("false")) multiplexer_93 (
    .in0(data_pass_translated_up), .in1({32{1'b0}}), .out(multiplexer_93_out), .sel(data_pass[7]));
  Multiplexer #(.width(32), .enable("false")) multiplexer_94 (
    .in0({32{1'b0}}), .in1(data_pass_translated_down), .out(multiplexer_94_out), .sel(data_pass[7]));
  Multiplexer #(.width(32), .enable("false")) multiplexer_95 (
    .in0(data_pass_translated_up), .in1({32{1'b0}}), .out(multiplexer_95_out), .sel(data_pass[7]));
  Multiplexer #(.width(32), .enable("false")) multiplexer_96 (
    .in0({32{1'b0}}), .in1(data_pass_translated_down), .out(multiplexer_96_out), .sel(data_pass[7]));
  Multiplexer #(.width(32), .enable("false")) multiplexer_97 (
    .in0(data_pass_translated_up), .in1({32{1'b0}}), .out(multiplexer_97_out), .sel(data_pass[7]));
  Multiplexer #(.width(32), .enable("false")) multiplexer_98 (
    .in0({32{1'b0}}), .in1(data_pass_translated_down), .out(multiplexer_98_out), .sel(data_pass[7]));
  Multiplexer #(.width(32), .enable("false")) multiplexer_99 (
    .in0(data_pass_translated_up), .in1({32{1'b0}}), .out(multiplexer_99_out), .sel(data_pass[7]));
  Multiplexer #(.width(32), .enable("false")) multiplexer_100 (
    .in0({32{1'b0}}), .in1(data_pass_translated_down), .out(multiplexer_100_out), .sel(data_pass[7]));
  Multiplexer #(.width(32), .enable("false")) multiplexer_101 (
    .in0(data_pass_translated_up), .in1({32{1'b0}}), .out(multiplexer_101_out), .sel(data_pass[7]));
  Multiplexer #(.width(32), .enable("false")) multiplexer_102 (
    .in0({32{1'b0}}), .in1(data_pass_translated_down), .out(multiplexer_102_out), .sel(data_pass[7]));
  Multiplexer #(.width(32), .enable("false")) multiplexer_103 (
    .in0(data_pass_translated_up), .in1({32{1'b0}}), .out(multiplexer_103_out), .sel(data_pass[7]));
  Multiplexer #(.width(32), .enable("false")) multiplexer_104 (
    .in0({32{1'b0}}), .in1(data_pass_translated_down), .out(multiplexer_104_out), .sel(data_pass[7]));
  Multiplexer #(.width(32), .enable("false")) multiplexer_105 (
    .in0(data_pass_translated_up), .in1({32{1'b0}}), .out(multiplexer_105_out), .sel(data_pass[7]));
  Multiplexer #(.width(32), .enable("false")) multiplexer_106 (
    .in0({32{1'b0}}), .in1(data_pass_translated_down), .out(multiplexer_106_out), .sel(data_pass[7]));
  // Probe on multiplexer_73_out
  // Probe on multiplexer_74_out
  // Probe on multiplexer_75_out
  // Probe on multiplexer_76_out
  // Probe on multiplexer_77_out
  // Probe on multiplexer_78_out
  // Probe on multiplexer_79_out
  // Probe on multiplexer_80_out
  // Probe on multiplexer_81_out
  // Probe on multiplexer_82_out
  // Probe on multiplexer_83_out
  // Probe on multiplexer_84_out
  // Probe on multiplexer_85_out
  // Probe on multiplexer_86_out
  // Probe on multiplexer_87_out
  // Probe on multiplexer_88_out
  // Probe on multiplexer_89_out
  // Probe on multiplexer_90_out
  // Probe on multiplexer_91_out
  // Probe on multiplexer_92_out
  // Probe on multiplexer_93_out
  // Probe on multiplexer_94_out
  // Probe on multiplexer_95_out
  // Probe on multiplexer_96_out
  // Probe on multiplexer_97_out
  // Probe on multiplexer_98_out
  // Probe on multiplexer_99_out
  // Probe on multiplexer_100_out
  // Probe on multiplexer_101_out
  // Probe on multiplexer_102_out
  // Probe on multiplexer_103_out
  // Probe on multiplexer_104_out
  // Probe on multiplexer_105_out
  // Probe on multiplexer_106_out
  Register #(.width(32)) register_73 (.D(multiplexer_73_out), .en(trig_2_1), .Q(led3_1), .clk(trig_2_1));  // open: clr
  Register #(.width(32)) register_74 (.D(multiplexer_75_out), .en(trig_2_2), .Q(led3_2), .clk(trig_2_2));  // open: clr
  Register #(.width(32)) register_75 (.D(multiplexer_77_out), .en(trig_2_3), .Q(led3_3), .clk(trig_2_3));  // open: clr
  Register #(.width(32)) register_76 (.D(multiplexer_79_out), .en(trig_2_4), .Q(led3_4), .clk(trig_2_4));  // open: clr
  Register #(.width(32)) register_77 (.D(multiplexer_81_out), .en(trig_2_5), .Q(led3_5), .clk(trig_2_5));  // open: clr
  Register #(.width(32)) register_78 (.D(multiplexer_83_out), .en(trig_2_6), .Q(led3_6), .clk(trig_2_6));  // open: clr
  Register #(.width(32)) register_79 (.D(multiplexer_85_out), .en(trig_2_7), .Q(led3_7), .clk(trig_2_7));  // open: clr
  Register #(.width(32)) register_80 (.D(multiplexer_87_out), .en(trig_2_8), .Q(led3_8), .clk(trig_2_8));  // open: clr
  Register #(.width(32)) register_81 (.D(multiplexer_89_out), .en(trig_2_9), .Q(led3_9), .clk(trig_2_9));  // open: clr
  Register #(.width(32)) register_82 (
    .D(multiplexer_91_out), .en(trig_2_10), .Q(led3_10), .clk(trig_2_10));  // open: clr
  Register #(.width(32)) register_83 (
    .D(multiplexer_93_out), .en(trig_2_11), .Q(led3_11), .clk(trig_2_11));  // open: clr
  Register #(.width(32)) register_84 (
    .D(multiplexer_95_out), .en(trig_2_12), .Q(led3_12), .clk(trig_2_12));  // open: clr
  Register #(.width(32)) register_85 (
    .D(multiplexer_97_out), .en(trig_2_13), .Q(led3_13), .clk(trig_2_13));  // open: clr
  Register #(.width(32)) register_86 (
    .D(multiplexer_99_out), .en(trig_2_14), .Q(led3_14), .clk(trig_2_14));  // open: clr
  Register #(.width(32)) register_87 (
    .D(multiplexer_101_out), .en(trig_2_15), .Q(led3_15), .clk(trig_2_15));  // open: clr
  Register #(.width(32)) register_88 (
    .D(multiplexer_103_out), .en(trig_2_16), .Q(led3_16), .clk(trig_2_16));  // open: clr
  Register #(.width(32)) register_89 (
    .D(multiplexer_105_out), .en(trig_2_17), .Q(led3_17), .clk(trig_2_17));  // open: clr
  Register #(.width(32)) register_90 (.D(multiplexer_74_out), .en(trig_2_1), .Q(led4_1), .clk(trig_2_1));  // open: clr
  Register #(.width(32)) register_91 (.D(multiplexer_76_out), .en(trig_2_2), .Q(led4_2), .clk(trig_2_2));  // open: clr
  Register #(.width(32)) register_92 (.D(multiplexer_78_out), .en(trig_2_3), .Q(led4_3), .clk(trig_2_3));  // open: clr
  Register #(.width(32)) register_93 (.D(multiplexer_80_out), .en(trig_2_4), .Q(led4_4), .clk(trig_2_4));  // open: clr
  Register #(.width(32)) register_94 (.D(multiplexer_82_out), .en(trig_2_5), .Q(led4_5), .clk(trig_2_5));  // open: clr
  Register #(.width(32)) register_95 (.D(multiplexer_84_out), .en(trig_2_6), .Q(led4_6), .clk(trig_2_6));  // open: clr
  Register #(.width(32)) register_96 (.D(multiplexer_86_out), .en(trig_2_7), .Q(led4_7), .clk(trig_2_7));  // open: clr
  Register #(.width(32)) register_97 (.D(multiplexer_88_out), .en(trig_2_8), .Q(led4_8), .clk(trig_2_8));  // open: clr
  Register #(.width(32)) register_98 (.D(multiplexer_90_out), .en(trig_2_9), .Q(led4_9), .clk(trig_2_9));  // open: clr
  Register #(.width(32)) register_99 (
    .D(multiplexer_92_out), .en(trig_2_10), .Q(led4_10), .clk(trig_2_10));  // open: clr
  Register #(.width(32)) register_100 (
    .D(multiplexer_94_out), .en(trig_2_11), .Q(led4_11), .clk(trig_2_11));  // open: clr
  Register #(.width(32)) register_101 (
    .D(multiplexer_96_out), .en(trig_2_12), .Q(led4_12), .clk(trig_2_12));  // open: clr
  Register #(.width(32)) register_102 (
    .D(multiplexer_98_out), .en(trig_2_13), .Q(led4_13), .clk(trig_2_13));  // open: clr
  Register #(.width(32)) register_103 (
    .D(multiplexer_100_out), .en(trig_2_14), .Q(led4_14), .clk(trig_2_14));  // open: clr
  Register #(.width(32)) register_104 (
    .D(multiplexer_102_out), .en(trig_2_15), .Q(led4_15), .clk(trig_2_15));  // open: clr
  Register #(.width(32)) register_105 (
    .D(multiplexer_104_out), .en(trig_2_16), .Q(led4_16), .clk(trig_2_16));  // open: clr
  Register #(.width(32)) register_106 (
    .D(multiplexer_106_out), .en(trig_2_17), .Q(led4_17), .clk(trig_2_17));  // open: clr
  // Probe on multiplexer_107_out
  Multiplexer #(.width(32), .enable("false")) multiplexer_107 (
    .in0(data_pass_translated_up), .in1({32{1'b0}}), .out(multiplexer_107_out), .sel(data_pass[7]));
  // Probe on multiplexer_108_out
  Multiplexer #(.width(32), .enable("false")) multiplexer_108 (
    .in0({32{1'b0}}), .in1(data_pass_translated_down), .out(multiplexer_108_out), .sel(data_pass[7]));
  // Probe on multiplexer_109_out
  Multiplexer #(.width(32), .enable("false")) multiplexer_109 (
    .in0(data_pass_translated_up), .in1({32{1'b0}}), .out(multiplexer_109_out), .sel(data_pass[7]));
  // Probe on multiplexer_110_out
  Multiplexer #(.width(32), .enable("false")) multiplexer_110 (
    .in0({32{1'b0}}), .in1(data_pass_translated_down), .out(multiplexer_110_out), .sel(data_pass[7]));
  // Probe on multiplexer_111_out
  Multiplexer #(.width(32), .enable("false")) multiplexer_111 (
    .in0(data_pass_translated_up), .in1({32{1'b0}}), .out(multiplexer_111_out), .sel(data_pass[7]));
  // Probe on multiplexer_112_out
  Multiplexer #(.width(32), .enable("false")) multiplexer_112 (
    .in0({32{1'b0}}), .in1(data_pass_translated_down), .out(multiplexer_112_out), .sel(data_pass[7]));
  // Probe on multiplexer_113_out
  Multiplexer #(.width(32), .enable("false")) multiplexer_113 (
    .in0(data_pass_translated_up), .in1({32{1'b0}}), .out(multiplexer_113_out), .sel(data_pass[7]));
  // Probe on multiplexer_114_out
  Multiplexer #(.width(32), .enable("false")) multiplexer_114 (
    .in0({32{1'b0}}), .in1(data_pass_translated_down), .out(multiplexer_114_out), .sel(data_pass[7]));
  // Probe on multiplexer_115_out
  Multiplexer #(.width(32), .enable("false")) multiplexer_115 (
    .in0(data_pass_translated_up), .in1({32{1'b0}}), .out(multiplexer_115_out), .sel(data_pass[7]));
  // Probe on multiplexer_116_out
  Multiplexer #(.width(32), .enable("false")) multiplexer_116 (
    .in0({32{1'b0}}), .in1(data_pass_translated_down), .out(multiplexer_116_out), .sel(data_pass[7]));
  // Probe on multiplexer_117_out
  Multiplexer #(.width(32), .enable("false")) multiplexer_117 (
    .in0(data_pass_translated_up), .in1({32{1'b0}}), .out(multiplexer_117_out), .sel(data_pass[7]));
  // Probe on multiplexer_118_out
  Multiplexer #(.width(32), .enable("false")) multiplexer_118 (
    .in0({32{1'b0}}), .in1(data_pass_translated_down), .out(multiplexer_118_out), .sel(data_pass[7]));
  // Probe on multiplexer_119_out
  Multiplexer #(.width(32), .enable("false")) multiplexer_119 (
    .in0(data_pass_translated_up), .in1({32{1'b0}}), .out(multiplexer_119_out), .sel(data_pass[7]));
  // Probe on multiplexer_120_out
  Multiplexer #(.width(32), .enable("false")) multiplexer_120 (
    .in0({32{1'b0}}), .in1(data_pass_translated_down), .out(multiplexer_120_out), .sel(data_pass[7]));
  // Probe on multiplexer_121_out
  Multiplexer #(.width(32), .enable("false")) multiplexer_121 (
    .in0(data_pass_translated_up), .in1({32{1'b0}}), .out(multiplexer_121_out), .sel(data_pass[7]));
  // Probe on multiplexer_122_out
  Multiplexer #(.width(32), .enable("false")) multiplexer_122 (
    .in0({32{1'b0}}), .in1(data_pass_translated_down), .out(multiplexer_122_out), .sel(data_pass[7]));
  // Probe on multiplexer_123_out
  Multiplexer #(.width(32), .enable("false")) multiplexer_123 (
    .in0(data_pass_translated_up), .in1({32{1'b0}}), .out(multiplexer_123_out), .sel(data_pass[7]));
  // Probe on multiplexer_124_out
  Multiplexer #(.width(32), .enable("false")) multiplexer_124 (
    .in0({32{1'b0}}), .in1(data_pass_translated_down), .out(multiplexer_124_out), .sel(data_pass[7]));
  // Probe on multiplexer_125_out
  Multiplexer #(.width(32), .enable("false")) multiplexer_125 (
    .in0(data_pass_translated_up), .in1({32{1'b0}}), .out(multiplexer_125_out), .sel(data_pass[7]));
  // Probe on multiplexer_126_out
  Multiplexer #(.width(32), .enable("false")) multiplexer_126 (
    .in0({32{1'b0}}), .in1(data_pass_translated_down), .out(multiplexer_126_out), .sel(data_pass[7]));
  // Probe on multiplexer_127_out
  Multiplexer #(.width(32), .enable("false")) multiplexer_127 (
    .in0(data_pass_translated_up), .in1({32{1'b0}}), .out(multiplexer_127_out), .sel(data_pass[7]));
  // Probe on multiplexer_128_out
  Multiplexer #(.width(32), .enable("false")) multiplexer_128 (
    .in0({32{1'b0}}), .in1(data_pass_translated_down), .out(multiplexer_128_out), .sel(data_pass[7]));
  // Probe on multiplexer_129_out
  Multiplexer #(.width(32), .enable("false")) multiplexer_129 (
    .in0(data_pass_translated_up), .in1({32{1'b0}}), .out(multiplexer_129_out), .sel(data_pass[7]));
  // Probe on multiplexer_130_out
  Multiplexer #(.width(32), .enable("false")) multiplexer_130 (
    .in0({32{1'b0}}), .in1(data_pass_translated_down), .out(multiplexer_130_out), .sel(data_pass[7]));
  // Probe on multiplexer_131_out
  Multiplexer #(.width(32), .enable("false")) multiplexer_131 (
    .in0(data_pass_translated_up), .in1({32{1'b0}}), .out(multiplexer_131_out), .sel(data_pass[7]));
  // Probe on multiplexer_132_out
  Multiplexer #(.width(32), .enable("false")) multiplexer_132 (
    .in0({32{1'b0}}), .in1(data_pass_translated_down), .out(multiplexer_132_out), .sel(data_pass[7]));
  // Probe on multiplexer_133_out
  Multiplexer #(.width(32), .enable("false")) multiplexer_133 (
    .in0(data_pass_translated_up), .in1({32{1'b0}}), .out(multiplexer_133_out), .sel(data_pass[7]));
  // Probe on multiplexer_134_out
  Multiplexer #(.width(32), .enable("false")) multiplexer_134 (
    .in0({32{1'b0}}), .in1(data_pass_translated_down), .out(multiplexer_134_out), .sel(data_pass[7]));
  // Probe on multiplexer_135_out
  Multiplexer #(.width(32), .enable("false")) multiplexer_135 (
    .in0(data_pass_translated_up), .in1({32{1'b0}}), .out(multiplexer_135_out), .sel(data_pass[7]));
  // Probe on multiplexer_136_out
  Multiplexer #(.width(32), .enable("false")) multiplexer_136 (
    .in0({32{1'b0}}), .in1(data_pass_translated_down), .out(multiplexer_136_out), .sel(data_pass[7]));
  Register #(.width(32)) register_107 (
    .D(multiplexer_107_out), .en(trig_2_18), .Q(led3_18), .clk(trig_2_18));  // open: clr
  Register #(.width(32)) register_108 (
    .D(multiplexer_108_out), .en(trig_2_18), .Q(led4_18), .clk(trig_2_18));  // open: clr
  Register #(.width(32)) register_109 (
    .D(multiplexer_109_out), .en(trig_2_19), .Q(led3_19), .clk(trig_2_19));  // open: clr
  Register #(.width(32)) register_110 (
    .D(multiplexer_110_out), .en(trig_2_19), .Q(led4_19), .clk(trig_2_19));  // open: clr
  Register #(.width(32)) register_111 (
    .D(multiplexer_111_out), .en(trig_2_20), .Q(led3_20), .clk(trig_2_20));  // open: clr
  Register #(.width(32)) register_112 (
    .D(multiplexer_112_out), .en(trig_2_20), .Q(led4_20), .clk(trig_2_20));  // open: clr
  Register #(.width(32)) register_113 (
    .D(multiplexer_113_out), .en(trig_2_21), .Q(led3_21), .clk(trig_2_21));  // open: clr
  Register #(.width(32)) register_114 (
    .D(multiplexer_114_out), .en(trig_2_21), .Q(led4_21), .clk(trig_2_21));  // open: clr
  Register #(.width(32)) register_115 (
    .D(multiplexer_115_out), .en(trig_2_22), .Q(led3_22), .clk(trig_2_22));  // open: clr
  Register #(.width(32)) register_116 (
    .D(multiplexer_116_out), .en(trig_2_22), .Q(led4_22), .clk(trig_2_22));  // open: clr
  Register #(.width(32)) register_117 (
    .D(multiplexer_117_out), .en(trig_2_23), .Q(led3_23), .clk(trig_2_23));  // open: clr
  Register #(.width(32)) register_118 (
    .D(multiplexer_118_out), .en(trig_2_23), .Q(led4_23), .clk(trig_2_23));  // open: clr
  Register #(.width(32)) register_119 (
    .D(multiplexer_119_out), .en(trig_2_24), .Q(led3_24), .clk(trig_2_24));  // open: clr
  Register #(.width(32)) register_120 (
    .D(multiplexer_120_out), .en(trig_2_24), .Q(led4_24), .clk(trig_2_24));  // open: clr
  Register #(.width(32)) register_121 (
    .D(multiplexer_121_out), .en(trig_2_25), .Q(led3_25), .clk(trig_2_25));  // open: clr
  Register #(.width(32)) register_122 (
    .D(multiplexer_122_out), .en(trig_2_25), .Q(led4_25), .clk(trig_2_25));  // open: clr
  Register #(.width(32)) register_123 (
    .D(multiplexer_123_out), .en(trig_2_26), .Q(led3_26), .clk(trig_2_26));  // open: clr
  Register #(.width(32)) register_124 (
    .D(multiplexer_124_out), .en(trig_2_26), .Q(led4_26), .clk(trig_2_26));  // open: clr
  Register #(.width(32)) register_125 (
    .D(multiplexer_125_out), .en(trig_2_27), .Q(led3_27), .clk(trig_2_27));  // open: clr
  Register #(.width(32)) register_126 (
    .D(multiplexer_126_out), .en(trig_2_27), .Q(led4_27), .clk(trig_2_27));  // open: clr
  Register #(.width(32)) register_127 (
    .D(multiplexer_127_out), .en(trig_2_28), .Q(led3_28), .clk(trig_2_28));  // open: clr
  Register #(.width(32)) register_128 (
    .D(multiplexer_128_out), .en(trig_2_28), .Q(led4_28), .clk(trig_2_28));  // open: clr
  Register #(.width(32)) register_129 (
    .D(multiplexer_129_out), .en(trig_2_29), .Q(led3_29), .clk(trig_2_29));  // open: clr
  Register #(.width(32)) register_130 (
    .D(multiplexer_130_out), .en(trig_2_29), .Q(led4_29), .clk(trig_2_29));  // open: clr
  Register #(.width(32)) register_131 (
    .D(multiplexer_131_out), .en(trig_2_30), .Q(led3_30), .clk(trig_2_30));  // open: clr
  Register #(.width(32)) register_132 (
    .D(multiplexer_132_out), .en(trig_2_30), .Q(led4_30), .clk(trig_2_30));  // open: clr
  Register #(.width(32)) register_133 (
    .D(multiplexer_133_out), .en(trig_2_31), .Q(led3_31), .clk(trig_2_31));  // open: clr
  Register #(.width(32)) register_134 (
    .D(multiplexer_134_out), .en(trig_2_31), .Q(led4_31), .clk(trig_2_31));  // open: clr
  Register #(.width(32)) register_135 (
    .D(multiplexer_135_out), .en(trig_2_32), .Q(led3_32), .clk(trig_2_32), .clr(trig_2_32));
  Register #(.width(32)) register_136 (
    .D(multiplexer_136_out), .en(trig_2_32), .Q(led4_32), .clk(trig_2_32));  // open: clr

  // Other names for the same wires on the sheet: Coef1Res[3:0] = Coef1; Coef2Res[3:0] = Coef2; Coef3Res[3:0] = Coef3;
  //   trig_up_down = data_pass[7]; rd_wr_prime = In_out_prime

  // Notes on the sheet:
  //   UI CIRCUITS
  //   Coefficient 1 Display
  //   Inc
  //   Coefficient 2 Display
  //   Inc
  //   Constant Display
  //   Inc
  //   Stays between 0-9
  //   Stays between 0-9
  //   Stays between 0-9
  //   memory-mapped I/O
  //   Result for Equation
  //   Result for Equation
  //   Result for Equation
  //   CHOICE ADDER
  //   Passing Values to Processor
  //   DATA FETCHER
  //   Pass Calculated Value and Count
  //   instr memory
  //   contents of rom_1 (hex, n*v repeats v):
  //   cd f0 d0 f0 b1 c1 b1 c1 b1 c1 35 3a d1 e0 d2 20 79 eb 3c 3a cc 2 c6 cc fd d6 3c c c6 18 0 e1 23 ee
  //   24 84 c6 cc fc 0 e4 2e d6 4c ee 30 d6 60 cd f0 d2 f0 ab d2 20 8d cd ed ee 10 c1 30 d0 1 3f d3 0 72
  //   ec 4a 17 8c ee 43 c5 d7 c0 c1 3f d3 0 72 eb 5d 86 18 86 8f d1 c0 a7 ee 51 c5 c4 d7 c0 c1 3f d3 0 84
  //   72 eb 72 86 18 86 8f d1 c0 a7 ee 66 87 c5 c4 d7
  //   data memory
  //   X
  //   +
  //   Y
  //   +
  //   =
  //   0
  //   16
  //   24
  //   32
  //   Upper LED
  //   Translators
  //   -16
  //   Lower LED
  //   1-2 LEDS
  //   Triggers
  //   3-4 LEDS
  //   Raising System - LED 1&2
  //   Raising System - LED 3&4
endmodule

module inc (
  input  [7:0] X,
  output [7:0] R,
  output Cout
);

  wire [7:1] and_1_out;

  assign {Cout, and_1_out} = {and_1_out, 1'b1} & X;  // AND_Gate and_1, 8 bits wide
  assign R = X ^ {and_1_out, 1'b1};  // XOR_Gate xor_1, 8 bits wide
endmodule
